// Logisim project Run 1.circ as structural Verilog: 1 circuit, main circuit main
module main (
  input  Clk,
  input  Input,
  input  Sel_Line,
  output Q0,
  output Q1,
  output Q2,
  output Q3
);

  wire multiplexer_1_out, multiplexer_2_out, multiplexer_3_out, not_1_out, t_ff_1_qn, t_ff_2_qn, t_ff_3_qn;

  not not_1 (not_1_out, Clk);
  T_Flip_Flop t_ff_1 (.clk(not_1_out), .T(Input), .Q(Q0), .Qn(t_ff_1_qn));  // open: preset, reset, en
  Multiplexer multiplexer_1 (.in0(Q0), .in1(t_ff_1_qn), .out(multiplexer_1_out), .sel(Sel_Line));  // open: en
  T_Flip_Flop t_ff_2 (.clk(multiplexer_1_out), .T(Input), .Q(Q1), .Qn(t_ff_2_qn));  // open: preset, reset, en
  Multiplexer multiplexer_2 (.in0(Q1), .in1(t_ff_2_qn), .out(multiplexer_2_out), .sel(Sel_Line));  // open: en
  T_Flip_Flop t_ff_3 (.clk(multiplexer_2_out), .T(Input), .Q(Q2), .Qn(t_ff_3_qn));  // open: preset, reset, en
  Multiplexer multiplexer_3 (.in0(Q2), .in1(t_ff_3_qn), .out(multiplexer_3_out), .sel(Sel_Line));  // open: en
  T_Flip_Flop t_ff_4 (.clk(multiplexer_3_out), .T(Input), .Q(Q3));  // open: Qn, preset, reset, en

  // Notes on the sheet:
  //   2019A7PS0020U
  //   MOD 16 Counter
  //   Dhruv Maheshwari
endmodule
