// Logisim project Run 2.circ as structural Verilog: 1 circuit, main circuit main
module main (
  input  Clk,
  input  Input,
  output Q0,
  output Q1,
  output Q2,
  output Q3
);

  wire not_1_out, Q3_Q1_out, t_ff_1_qn, t_ff_2_qn, t_ff_3_qn;

  not not_1 (not_1_out, Clk);
  T_Flip_Flop t_ff_1 (.clk(not_1_out), .T(Input), .Q(Q0), .Qn(t_ff_1_qn), .reset(Q3_Q1_out));  // open: preset, en
  T_Flip_Flop t_ff_2 (.clk(t_ff_1_qn), .T(Input), .Q(Q1), .Qn(t_ff_2_qn), .reset(Q3_Q1_out));  // open: preset, en
  and Q3_Q1 (Q3_Q1_out, Q1, Q3);
  T_Flip_Flop t_ff_3 (.clk(t_ff_2_qn), .T(Input), .Q(Q2), .Qn(t_ff_3_qn), .reset(Q3_Q1_out));  // open: preset, en
  T_Flip_Flop t_ff_4 (.clk(t_ff_3_qn), .T(Input), .Q(Q3), .reset(Q3_Q1_out));  // open: Qn, preset, en

  // Notes on the sheet:
  //   2019A7PS0020U
  //   MOD 10 Counter
  //   Dhruv Maheshwari
endmodule
