// Logisim project Report_Q1.circ as structural Verilog: 1 circuit, main circuit main
module main (
  input  A,
  input  C,
  input  B,
  output X
);

  wire and_1_out, and_2_out, not_1_out;

  and and_1 (and_1_out, A, C);
  not not_1 (not_1_out, C);
  and and_2 (and_2_out, not_1_out, B);
  or or_1 (X, and_1_out, and_2_out);

  // Notes on the sheet:
  //   P
  //   Q
  //   R
  //   X
endmodule
