// Logisim project Report_Q2.circ as structural Verilog: 1 circuit, main circuit main
module main (
  input  A,
  input  B,
  input  C,
  input  D,
  input  L,
  output F
);

  wire xor_1_out, xor_2_out, xor_3_out;

  xor xor_1 (xor_1_out, A, B);
  xor xor_2 (xor_2_out, xor_1_out, C);
  xor xor_3 (xor_3_out, xor_2_out, D);
  xor xor_4 (F, xor_3_out, L);
endmodule
