// Logisim project half adder.circ as structural Verilog: 1 circuit, main circuit main
module main (
  input  A,
  input  B,
  output SUM,
  output CARRY
);

  xor u_SUM (SUM, A, B);
  and u_CARRY (CARRY, A, B);

  // Notes on the sheet:
  //   HALF ADDER
endmodule
