// Logisim project half subtractor.circ as structural Verilog: 1 circuit, main circuit main
module main (
  input  A,
  input  B,
  output DIFF,
  output BORROW
);

  wire not_1_out;

  not not_1 (not_1_out, A);
  xor u_DIFF (DIFF, A, B);
  and and_1 (BORROW, not_1_out, B);

  // Notes on the sheet:
  //   Half subtractor
endmodule
