// Logisim project Run 1.circ as structural Verilog: 1 circuit, main circuit main
module main (
  input  [3:0] A0,
  input  [3:0] B0
);

  wire comparator_1_eq, comparator_1_gt, comparator_1_lt;

  Comparator #(.width(4)) comparator_1 (
    .a(A0), .b(B0), .gt(comparator_1_gt), .eq(comparator_1_eq), .lt(comparator_1_lt));
  DotMatrix #(.matrixcols(3), .matrixrows(1)) dotmatrix_1 (
    .col0(comparator_1_gt), .col1(comparator_1_eq), .col2(comparator_1_lt));

  // Notes on the sheet:
  //   A2
  //   A3
  //   B2
  //   B1
  //   B3
  //   Dhruv Maheshwari
  //   2019A7PS0020U
  //   Comaprator
  //   A1
endmodule
