// Logisim project Run 2.circ as structural Verilog: 1 circuit, main circuit main
module main (
  input  E,
  input  [2:0] in_2
);

  wire decoder_1_out0, decoder_1_out1, decoder_1_out2, decoder_1_out3, decoder_1_out4, decoder_1_out5,
       decoder_1_out6, decoder_1_out7;

  Decoder #(.select(3)) decoder_1 (
    .out0(decoder_1_out0), .out1(decoder_1_out1), .out2(decoder_1_out2), .out3(decoder_1_out3),
    .out4(decoder_1_out4), .out5(decoder_1_out5), .out6(decoder_1_out6), .out7(decoder_1_out7), .sel(in_2),
    .en(E));
  LED led_1 (.in(decoder_1_out0));
  LED led_2 (.in(decoder_1_out1));
  LED led_3 (.in(decoder_1_out2));
  LED led_4 (.in(decoder_1_out3));
  LED led_5 (.in(decoder_1_out4));
  LED led_6 (.in(decoder_1_out5));
  LED led_7 (.in(decoder_1_out6));
  LED led_8 (.in(decoder_1_out7));

  // Notes on the sheet:
  //   Dhruv Maheshwari
  //   2019A7PS0020U
  //   3:8 Decoder
  //   Y0
  //   Y1
  //   Y2
  //   Y3
  //   Y4
  //   Y5
  //   Y6
  //   Y7
endmodule
