// Logisim project Run 1.circ as structural Verilog: 1 circuit, main circuit main
module main (
  input  D0,
  input  D1,
  input  D2,
  input  D3,
  input  D4,
  input  D5,
  input  D6,
  input  E,
  input  D7,
  input  [2:0] in_10,
  output Output
);

  Multiplexer #(.select(3)) multiplexer_1 (
    .in0(D0), .in1(D1), .in2(D2), .in3(D3), .in4(D4), .in5(D5), .in6(D6), .in7(D7), .out(Output),
    .sel(in_10), .en(E));

  // Notes on the sheet:
  //   MUX
  //   Dhruv Maheshwari
  //   2019A7PS0020U
endmodule
