// Logisim project Run 2.circ as structural Verilog: 1 circuit, main circuit main
module main (
  input  Input,
  input  E,
  input  [2:0] in_3,
  output D0,
  output D1,
  output D2,
  output D3,
  output D4,
  output D5,
  output D6,
  output D7
);

  Demultiplexer #(.select(3)) demultiplexer_1 (
    .out0(D0), .out1(D1), .out2(D2), .out3(D3), .out4(D4), .out5(D5), .out6(D6), .out7(D7), .in(Input),
    .sel(in_3), .en(E));

  // Notes on the sheet:
  //   Dhruv Maheshwari
  //   2019A7PS0020U
  //   DEMUX
endmodule
