// Logisim project Run 1.circ as structural Verilog: 1 circuit, main circuit main
module main (
  input  S,
  input  R,
  output Q,
  output nQ
);

  wire CLK_out, nand_1_out, nand_2_out;

  Clock CLK (.out(CLK_out));
  nand nand_1 (nand_1_out, S, CLK_out);
  nand nand_2 (nand_2_out, CLK_out, R);
  nand nand_3 (Q, nand_1_out, nQ);
  nand nand_4 (nQ, Q, nand_2_out);

  // Notes on the sheet:
  //   Dhruv Maheshwari
  //   2019A7PS0020U
endmodule
