// Logisim project Run 2.circ as structural Verilog: 1 circuit, main circuit main
module main (
  input  J,
  input  K,
  input  Preset,
  input  Enable,
  input  Clear,
  output Q,
  output nQ
);

  wire clock_1_out, not_1_out, not_2_out;

  Clock clock_1 (.out(clock_1_out));
  not not_1 (not_1_out, Preset);
  not not_2 (not_2_out, Clear);
  J_K_Flip_Flop #(.trigger("falling")) j_k_ff_1 (
    .J(J), .clk(clock_1_out), .K(K), .Q(Q), .Qn(nQ), .preset(not_1_out), .en(Enable), .reset(not_2_out));

  // Notes on the sheet:
  //   Dhruv Maheshwari
  //   2019A7PS0020U
  //   Falling Edge
endmodule
