// Logisim project Run 3.circ as structural Verilog: 1 circuit, main circuit main
module main (
  input  T,
  input  PRESET,
  input  EN,
  input  CLEAR,
  output Q,
  output nQ
);

  wire CLK_out;

  Clock CLK (.out(CLK_out));
  J_K_Flip_Flop j_k_ff_1 (.J(T), .clk(CLK_out), .K(T), .Q(Q), .Qn(nQ), .preset(PRESET), .en(EN), .reset(CLEAR));

  // Notes on the sheet:
  //   Dhruv Maheshwari
  //   2019A7PS0020U
endmodule
