// Logisim project Run 1.circ as structural Verilog: 1 circuit, main circuit main
module main (
  input  X,
  input  in_2,
  output Z,
  output Q0,
  output Q1
);

  wire CLK_out, d_ff_1_qn;

  Clock CLK (.out(CLK_out));
  D_Flip_Flop d_ff_1 (.clk(CLK_out), .D(X), .Q(Q0), .Qn(d_ff_1_qn), .en(in_2));  // open: preset, reset
  D_Flip_Flop d_ff_2 (.clk(CLK_out), .D(d_ff_1_qn), .Q(Q1), .en(in_2));  // open: Qn, preset, reset
  and and_1 (Z, X, Q1);

  // Notes on the sheet:
  //   Dhruv Maheshwari
  //   2019A7PS0020U
endmodule
