// Logisim project Run 1.circ as structural Verilog: 1 circuit, main circuit main
module main (
  input  Reset,
  input  EN,
  input  [1:0] Select_Line,
  input  I0,
  input  I1,
  input  I2,
  input  I3,
  input  Right_shift,
  input  Left_shift,
  output A3,
  output A2,
  output A1,
  output A0
);

  wire CLK_out, multiplexer_1_out, multiplexer_2_out, multiplexer_3_out, multiplexer_4_out;

  Clock CLK (.out(CLK_out));
  Multiplexer #(.select(2)) multiplexer_1 (
    .in0(A3), .in1(Right_shift), .in2(A2), .in3(I0), .out(multiplexer_1_out), .sel(Select_Line), .en(EN));
  D_Flip_Flop d_ff_1 (.clk(CLK_out), .D(multiplexer_1_out), .Q(A3), .reset(Reset));  // open: Qn, preset, en
  Multiplexer #(.select(2)) multiplexer_2 (
    .in0(A2), .in1(A3), .in2(A1), .in3(I1), .out(multiplexer_2_out), .sel(Select_Line), .en(EN));
  D_Flip_Flop d_ff_2 (.clk(CLK_out), .D(multiplexer_2_out), .Q(A2), .reset(Reset));  // open: Qn, preset, en
  Multiplexer #(.select(2)) multiplexer_3 (
    .in0(A1), .in1(A2), .in2(A0), .in3(I2), .out(multiplexer_3_out), .sel(Select_Line), .en(EN));
  D_Flip_Flop d_ff_3 (.clk(CLK_out), .D(multiplexer_3_out), .Q(A1), .reset(Reset));  // open: Qn, preset, en
  D_Flip_Flop d_ff_4 (.clk(CLK_out), .D(multiplexer_4_out), .Q(A0), .reset(Reset));  // open: Qn, preset, en
  Multiplexer #(.select(2)) multiplexer_4 (
    .in0(A0), .in1(A1), .in2(Left_shift), .in3(I3), .out(multiplexer_4_out), .sel(Select_Line), .en(EN));
endmodule
